// Logisim project kib 2.circ as structural Verilog: 1 circuit, main circuit main
module main (
  input  in_1,
  input  in_2,
  input  in_3,
  input  in_4,
  input  in_5,
  input  in_6,
  input  in_7,
  input  in_8,
  input  in_9
);

  wire transistor_1_out, transistor_2_out, transistor_3_out, transistor_5_out, transistor_8_out,
       transistor_9_out, transistor_10_out, transistor_12_out, transistor_16_out;

  Transistor #(.\type ("n")) transistor_1 (.in(1'b1), .out(transistor_1_out), .gate(in_2));
  Transistor transistor_2 (.in(1'b0), .out(transistor_2_out), .gate(in_5));
  Transistor #(.\type ("n")) transistor_3 (.in(1'b1), .out(transistor_3_out), .gate(in_4));
  Transistor #(.\type ("n")) transistor_4 (.in(1'b1), .out(transistor_3_out), .gate(in_5));
  Transistor transistor_5 (.in(1'b1), .out(transistor_5_out), .gate(in_6));
  Transistor transistor_6 (.in(1'b1), .out(transistor_5_out), .gate(in_7));
  Transistor #(.\type ("n")) transistor_7 (.in(transistor_8_out), .out(transistor_5_out), .gate(in_7));
  Transistor #(.\type ("n")) transistor_8 (.in(1'b0), .out(transistor_8_out), .gate(in_6));
  Transistor transistor_9 (.in(1'b1), .out(transistor_9_out), .gate(in_9));
  Transistor transistor_10 (.in(1'b1), .out(transistor_10_out), .gate(in_1));
  Transistor #(.\type ("n")) transistor_11 (.in(1'b0), .out(transistor_10_out), .gate(in_1));
  Transistor transistor_12 (.in(1'b0), .out(transistor_12_out), .gate(in_2));
  Transistor transistor_13 (.in(1'b0), .out(transistor_12_out), .gate(in_3));
  Transistor #(.\type ("n")) transistor_14 (.in(transistor_1_out), .out(transistor_12_out), .gate(in_3));
  Transistor transistor_15 (.in(transistor_2_out), .out(transistor_3_out), .gate(in_4));
  LED led_1 (.in(transistor_3_out));
  Transistor transistor_16 (.in(transistor_9_out), .out(transistor_16_out), .gate(in_8));
  Transistor #(.\type ("n")) transistor_17 (.in(1'b0), .out(transistor_16_out), .gate(in_8));
  Transistor #(.\type ("n")) transistor_18 (.in(1'b0), .out(transistor_16_out), .gate(in_9));
  LED led_2 (.in(transistor_10_out));
  LED led_3 (.in(transistor_5_out));
  LED led_4 (.in(transistor_16_out));
  LED led_5 (.in(transistor_12_out));
endmodule
